// Logisim project model.circ as structural Verilog: 1 circuit, main circuit main
module main (
  input  [1:0] in_1,
  input  in_2,
  input  [1:0] in_3,
  input  in_4,
  output [1:0] out_5,
  output [1:0] out_6
);

  wire and_1_out, and_2_out, and_3_out, and_4_out, and_5_out, and_6_out, and_7_out, and_8_out, and_9_out,
       and_10_out, and_11_out, and_12_out, and_13_out, and_14_out, and_15_out, and_16_out, and_17_out,
       and_18_out, and_19_out, and_20_out, and_21_out, and_22_out, and_23_out, and_24_out, and_25_out,
       and_26_out, and_27_out, and_28_out, and_29_out, and_30_out, and_31_out, and_32_out, and_33_out,
       and_34_out, and_35_out, and_36_out, and_37_out, and_38_out, and_39_out, and_40_out, and_41_out,
       and_42_out, and_43_out, and_44_out, and_45_out, and_46_out, and_47_out, and_48_out, and_49_out,
       and_50_out, and_51_out, and_52_out, button_1_out, button_2_out, button_3_out, button_4_out,
       button_5_out, button_6_out, button_7_out, button_8_out, button_9_out, button_10_out, button_11_out,
       button_12_out, clock_1_out, clock_2_out, clock_3_out, clock_4_out, clock_5_out, clock_6_out,
       clock_7_out, clock_8_out, clock_9_out, clock_10_out, clock_11_out, clock_12_out, comparator_1_gt,
       comparator_2_gt, counter_1_q, counter_2_q, d_ff_1_q, d_ff_4_q, d_ff_5_q, d_ff_6_q, d_ff_9_q,
       d_ff_10_q, d_ff_11_q, d_ff_12_q, decoder_1_out0, decoder_1_out1, decoder_1_out2, decoder_1_out3,
       decoder_2_out0, decoder_2_out1, decoder_2_out2, decoder_2_out3, decoder_3_out0, decoder_3_out1,
       decoder_3_out2, decoder_3_out3, decoder_4_out0, decoder_4_out1, decoder_4_out2, decoder_4_out3,
       decoder_5_out0, decoder_5_out1, decoder_6_out0, decoder_6_out1, decoder_7_out0, decoder_7_out1,
       decoder_7_out2, decoder_7_out3, decoder_8_out0, decoder_8_out1, decoder_8_out2, decoder_8_out3,
       decoder_9_out1, decoder_9_out2, decoder_9_out3, decoder_10_out1, decoder_10_out2, decoder_10_out3,
       decoder_11_out0, decoder_11_out1, decoder_11_out2, decoder_11_out3, decoder_12_out0, decoder_12_out1,
       decoder_12_out2, decoder_12_out3, multiplexer_3_out, multiplexer_6_out, nor_1_out, nor_2_out,
       nor_3_out, nor_4_out, nor_5_out, nor_6_out, not_1_out, not_2_out, not_3_out, not_4_out, not_5_out,
       not_6_out, or_1_out, or_2_out, or_3_out, or_4_out, or_5_out, or_6_out, or_7_out, or_8_out, or_9_out,
       or_10_out, or_11_out, or_12_out, or_13_out, or_14_out, or_15_out, or_16_out, or_17_out, or_18_out,
       or_19_out, or_20_out, or_21_out, or_22_out, or_23_out, or_24_out, register_1_q, register_2_q,
       register_3_q, register_4_q, register_5_q, register_6_q, register_7_q, register_8_q, register_9_q,
       register_10_q, register_11_q, register_12_q, register_13_q, register_14_q, register_15_q,
       register_16_q, register_17_q, register_18_q, register_19_q, register_20_q, register_21_q,
       register_22_q;
  wire [1:0] d_ff_3_q, d_ff_8_q, multiplexer_2_out, multiplexer_5_out, subtractor_1_out, subtractor_2_out,
       subtractor_3_out, subtractor_4_out;
  wire [3:0] adder_1_out, adder_2_out, counter_3_q, counter_4_q, counter_6_q, counter_7_q, counter_9_q,
       counter_10_q;
  wire [4:0] counter_5_q, counter_8_q;

  Clock clock_1 (.out(clock_1_out));
  Button button_1 (.out(button_1_out));
  Button button_2 (.out(button_2_out));
  Button button_3 (.out(button_3_out));
  Button button_4 (.out(button_4_out));
  Counter #(.width(1), .max('h1)) counter_1 (
    .D(and_5_out), .count(in_4), .Q(counter_1_q), .clk(clock_1_out), .clr(not_1_out));  // open: load, carry
  not not_1 (not_1_out, and_5_out);
  and and_1 (and_1_out, ~decoder_3_out3, button_1_out);  // AND_Gate
  and and_2 (and_2_out, ~decoder_3_out2, button_2_out);  // AND_Gate
  and and_3 (and_3_out, ~decoder_3_out1, button_3_out);  // AND_Gate
  and and_4 (and_4_out, ~decoder_3_out0, or_1_out);  // AND_Gate
  or or_1 (or_1_out, button_4_out, counter_1_q);
  and and_5 (and_5_out, ~register_5_q, ~register_6_q, ~register_7_q, ~register_8_q);  // AND_Gate
  Button button_5 (.out(button_5_out));
  Button button_6 (.out(button_6_out));
  Button button_7 (.out(button_7_out));
  Button button_8 (.out(button_8_out));
  Counter #(.width(1), .max('h1)) counter_2 (
    .D(and_10_out), .count(in_2), .Q(counter_2_q), .clk(clock_2_out), .clr(not_2_out));  // open: load, carry
  not not_2 (not_2_out, and_10_out);
  Clock clock_2 (.out(clock_2_out));
  Register #(.width(1)) register_1 (
    .D(and_1_out), .Q(register_1_q), .clk(and_1_out), .clr(decoder_1_out3));  // open: en
  Register #(.width(1)) register_2 (
    .D(and_2_out), .Q(register_2_q), .clk(and_2_out), .clr(decoder_1_out2));  // open: en
  Register #(.width(1)) register_3 (
    .D(and_3_out), .Q(register_3_q), .clk(and_3_out), .clr(decoder_1_out1));  // open: en
  Register #(.width(1)) register_4 (
    .D(and_4_out), .Q(register_4_q), .clk(and_4_out), .clr(decoder_1_out0));  // open: en
  or or_2 (or_2_out, button_8_out, counter_2_q);
  and and_6 (and_6_out, ~decoder_4_out3, button_5_out);  // AND_Gate
  and and_7 (and_7_out, ~decoder_4_out2, button_6_out);  // AND_Gate
  and and_8 (and_8_out, ~decoder_4_out1, button_7_out);  // AND_Gate
  and and_9 (and_9_out, ~decoder_4_out0, or_2_out);  // AND_Gate
  and and_10 (and_10_out, ~register_13_q, ~register_14_q, ~register_15_q, ~register_16_q);  // AND_Gate
  Register #(.width(1)) register_5 (
    .D(register_1_q), .Q(register_5_q), .clk(and_11_out), .clr(decoder_1_out3));  // open: en
  and and_11 (and_11_out, register_1_q, ~or_15_out);  // AND_Gate
  Register #(.width(1)) register_6 (
    .D(register_2_q), .Q(register_6_q), .clk(and_12_out), .clr(decoder_1_out2));  // open: en
  and and_12 (and_12_out, register_2_q, ~or_15_out);  // AND_Gate
  Register #(.width(1)) register_7 (
    .D(register_3_q), .Q(register_7_q), .clk(and_13_out), .clr(decoder_1_out1));  // open: en
  and and_13 (and_13_out, register_3_q, ~or_15_out);  // AND_Gate
  Register #(.width(1)) register_8 (
    .D(register_4_q), .Q(register_8_q), .clk(and_14_out), .clr(decoder_1_out0));  // open: en
  and and_14 (and_14_out, register_4_q, ~or_15_out);  // AND_Gate
  Decoder #(.select(2), .disabled(0)) decoder_1 (
    .out0(decoder_1_out0), .out1(decoder_1_out1), .out2(decoder_1_out2), .out3(decoder_1_out3),
    .sel(d_ff_3_q), .en(or_22_out));
  Register #(.width(1)) register_9 (
    .D(and_6_out), .Q(register_9_q), .clk(and_6_out), .clr(decoder_2_out3));  // open: en
  Register #(.width(1)) register_10 (
    .D(and_7_out), .Q(register_10_q), .clk(and_7_out), .clr(decoder_2_out2));  // open: en
  Register #(.width(1)) register_11 (
    .D(and_8_out), .Q(register_11_q), .clk(and_8_out), .clr(decoder_2_out1));  // open: en
  Register #(.width(1)) register_12 (
    .D(and_9_out), .Q(register_12_q), .clk(and_9_out), .clr(decoder_2_out0));  // open: en
  and and_15 (and_15_out, register_9_q, ~or_16_out);  // AND_Gate
  and and_16 (and_16_out, register_10_q, ~or_16_out);  // AND_Gate
  and and_17 (and_17_out, register_11_q, ~or_16_out);  // AND_Gate
  and and_18 (and_18_out, register_12_q, ~or_16_out);  // AND_Gate
  nor nor_1 (nor_1_out, register_8_q, register_7_q);
  Register #(.width(1)) register_13 (
    .D(register_9_q), .Q(register_13_q), .clk(and_15_out), .clr(decoder_2_out3));  // open: en
  Register #(.width(1)) register_14 (
    .D(register_10_q), .Q(register_14_q), .clk(and_16_out), .clr(decoder_2_out2));  // open: en
  Register #(.width(1)) register_15 (
    .D(register_11_q), .Q(register_15_q), .clk(and_17_out), .clr(decoder_2_out1));  // open: en
  Register #(.width(1)) register_16 (
    .D(register_12_q), .Q(register_16_q), .clk(and_18_out), .clr(decoder_2_out0));  // open: en
  Decoder #(.select(2), .disabled(0)) decoder_2 (
    .out0(decoder_2_out0), .out1(decoder_2_out1), .out2(decoder_2_out2), .out3(decoder_2_out3),
    .sel(d_ff_8_q), .en(or_24_out));
  Decoder #(.select(2), .enable("false")) decoder_3 (
    .out0(decoder_3_out0), .out1(decoder_3_out1), .out2(decoder_3_out2), .out3(decoder_3_out3), .sel(d_ff_3_q));
  not not_3 (not_3_out, register_7_q);
  or or_3 (or_3_out, ~register_6_q, register_7_q);  // OR_Gate
  nor nor_2 (nor_2_out, register_8_q, multiplexer_3_out);
  and and_19 (and_19_out, register_7_q, ~multiplexer_3_out);  // AND_Gate
  and and_20 (and_20_out, register_5_q, multiplexer_3_out);
  and and_21 (and_21_out, register_5_q, d_ff_4_q);
  nor nor_3 (nor_3_out, register_16_q, register_15_q);
  LED led_1 (.in(and_27_out));
  LED led_2 (.in(and_27_out));
  LED led_3 (.in(and_22_out));
  LED led_4 (.in(and_22_out));
  and and_22 (and_22_out, and_49_out, decoder_5_out0);
  and and_23 (and_23_out, ~register_6_q, register_7_q);  // AND_Gate
  not not_4 (not_4_out, register_6_q);
  or or_4 (or_4_out, and_19_out, and_20_out);
  and and_24 (and_24_out, nor_1_out, ~d_ff_4_q);  // AND_Gate
  Decoder #(.select(2), .enable("false")) decoder_4 (
    .out0(decoder_4_out0), .out1(decoder_4_out1), .out2(decoder_4_out2), .out3(decoder_4_out3), .sel(d_ff_8_q));
  not not_5 (not_5_out, register_15_q);
  nor nor_4 (nor_4_out, register_16_q, multiplexer_6_out);
  and and_25 (and_25_out, register_13_q, multiplexer_6_out);
  and and_26 (and_26_out, register_13_q, d_ff_9_q);
  LED led_5 (.in(and_49_out));
  LED led_6 (.in(and_27_out));
  LED led_7 (.in(and_27_out));
  LED led_8 (.in(and_49_out));
  LED led_9 (.in(and_22_out));
  LED led_10 (.in(and_49_out));
  LED led_11 (.in(and_49_out));
  LED led_12 (.in(and_22_out));
  and and_27 (and_27_out, decoder_5_out1, and_49_out);
  Decoder #(.enable("false")) decoder_5 (.out0(decoder_5_out0), .out1(decoder_5_out1), .sel(multiplexer_3_out));
  and and_28 (and_28_out, not_4_out, multiplexer_3_out);
  or or_5 (or_5_out, and_28_out, nor_2_out);
  or or_6 (or_6_out, register_6_q, register_5_q);
  and and_29 (and_29_out, or_6_out, d_ff_4_q);
  or or_7 (or_7_out, and_21_out, and_24_out);
  nor nor_5 (nor_5_out, d_ff_4_q, register_8_q);
  or or_8 (or_8_out, ~register_14_q, register_15_q);  // OR_Gate
  not not_6 (not_6_out, register_14_q);
  and and_30 (and_30_out, register_15_q, ~multiplexer_6_out);  // AND_Gate
  or or_9 (or_9_out, nor_5_out, and_29_out);
  LED led_13 (.in(and_52_out));
  LED led_14 (.in(and_35_out));
  LED led_15 (.in(and_35_out));
  LED led_16 (.in(and_35_out));
  LED led_17 (.in(and_52_out));
  LED led_18 (.in(and_31_out));
  LED led_19 (.in(and_52_out));
  LED led_20 (.in(and_52_out));
  LED led_21 (.in(and_31_out));
  LED led_22 (.in(and_31_out));
  and and_31 (and_31_out, and_52_out, decoder_6_out0);
  Decoder #(.enable("false")) decoder_6 (.out0(decoder_6_out0), .out1(decoder_6_out1), .sel(multiplexer_6_out));
  and and_32 (and_32_out, ~register_14_q, register_15_q);  // AND_Gate
  and and_33 (and_33_out, not_6_out, multiplexer_6_out);
  or or_10 (or_10_out, and_30_out, and_25_out);
  or or_11 (or_11_out, register_14_q, register_13_q);
  or or_12 (or_12_out, and_26_out, and_34_out);
  and and_34 (and_34_out, nor_3_out, ~d_ff_9_q);  // AND_Gate
  nor nor_6 (nor_6_out, d_ff_9_q, register_16_q);
  Hex_Digit_Display hex_digit_display_1 (.value(adder_1_out));  // open: dp
  Adder #(.width(4)) adder_1 (.a(4'b0001), .b({2'b00, d_ff_3_q}), .out(adder_1_out));  // open: cin, cout
  LED led_23 (.in(and_35_out));
  LED led_24 (.in(and_31_out));
  and and_35 (and_35_out, decoder_6_out1, and_52_out);
  or or_13 (or_13_out, and_33_out, nor_4_out);
  and and_36 (and_36_out, or_11_out, d_ff_9_q);
  Adder #(.width(4)) adder_2 (.a(4'b0001), .b({2'b00, d_ff_8_q}), .out(adder_2_out));  // open: cin, cout
  or or_14 (or_14_out, nor_6_out, and_36_out);
  LED led_25 (.in(decoder_7_out0));
  Multiplexer #(.select(2), .enable("false")) multiplexer_1 (
    .in0(not_3_out), .in1(multiplexer_3_out), .in2(multiplexer_3_out), .in3(register_6_q),
    .out(multiplexer_2_out[1]), .sel(d_ff_3_q));
  Multiplexer #(.select(2), .enable("false")) multiplexer_2 (
    .in0(or_3_out), .in1(or_5_out), .in2(or_4_out), .in3(and_23_out), .out(multiplexer_2_out[0]),
    .sel(d_ff_3_q));
  Multiplexer #(.select(2), .enable("false")) multiplexer_3 (
    .in0(1'b1), .in1(or_9_out), .in2(or_7_out), .in3(1'b0), .out(multiplexer_3_out), .sel(d_ff_3_q));
  Hex_Digit_Display hex_digit_display_2 (.value(adder_2_out));  // open: dp
  LED led_26 (.in(decoder_7_out1));
  Clock clock_3 (.out(clock_3_out));
  D_Flip_Flop #(.trigger("falling")) d_ff_1 (
    .clk(clock_3_out), .D(or_17_out), .Q(d_ff_1_q));  // open: Qn, preset, en, reset
  D_Flip_Flop #(.trigger("falling")) d_ff_2 (
    .clk(or_17_out), .D(multiplexer_2_out[1]), .Q(d_ff_3_q[1]));  // open: Qn, preset, en, reset
  D_Flip_Flop #(.trigger("falling")) d_ff_3 (
    .clk(or_17_out), .D(multiplexer_2_out[0]), .Q(d_ff_3_q[0]));  // open: Qn, preset, en, reset
  D_Flip_Flop #(.trigger("falling")) d_ff_4 (
    .clk(or_17_out), .D(multiplexer_3_out), .Q(d_ff_4_q));  // open: Qn, preset, en, reset
  Multiplexer #(.select(2), .enable("false")) multiplexer_4 (
    .in0(not_5_out), .in1(multiplexer_6_out), .in2(multiplexer_6_out), .in3(register_14_q),
    .out(multiplexer_5_out[1]), .sel(d_ff_8_q));
  Multiplexer #(.select(2), .enable("false")) multiplexer_5 (
    .in0(or_8_out), .in1(or_13_out), .in2(or_10_out), .in3(and_32_out), .out(multiplexer_5_out[0]),
    .sel(d_ff_8_q));
  Multiplexer #(.select(2), .enable("false")) multiplexer_6 (
    .in0(1'b1), .in1(or_14_out), .in2(or_12_out), .in3(1'b0), .out(multiplexer_6_out), .sel(d_ff_8_q));
  Decoder #(.select(2), .disabled(0)) decoder_7 (
    .out0(decoder_7_out0), .out1(decoder_7_out1), .out2(decoder_7_out2), .out3(decoder_7_out3),
    .sel(d_ff_3_q), .en(d_ff_5_q));
  D_Flip_Flop d_ff_5 (.clk(clock_3_out), .D(d_ff_1_q), .Q(d_ff_5_q));  // open: Qn, preset, en, reset
  LED led_27 (.in(decoder_8_out0));
  Clock clock_4 (.out(clock_4_out));
  LED led_28 (.in(decoder_7_out2));
  LED led_29 (.in(decoder_8_out1));
  D_Flip_Flop #(.trigger("falling")) d_ff_6 (
    .clk(clock_4_out), .D(or_19_out), .Q(d_ff_6_q));  // open: Qn, preset, en, reset
  D_Flip_Flop #(.trigger("falling")) d_ff_7 (
    .clk(or_19_out), .D(multiplexer_5_out[1]), .Q(d_ff_8_q[1]));  // open: Qn, preset, en, reset
  D_Flip_Flop #(.trigger("falling")) d_ff_8 (
    .clk(or_19_out), .D(multiplexer_5_out[0]), .Q(d_ff_8_q[0]));  // open: Qn, preset, en, reset
  D_Flip_Flop #(.trigger("falling")) d_ff_9 (
    .clk(or_19_out), .D(multiplexer_6_out), .Q(d_ff_9_q));  // open: Qn, preset, en, reset
  LED led_30 (.in(decoder_7_out3));
  Subtractor #(.width(2)) subtractor_1 (
    .a(d_ff_3_q), .b(multiplexer_2_out), .out(subtractor_1_out));  // open: bin, bout
  Subtractor #(.width(2)) subtractor_2 (
    .a(multiplexer_2_out), .b(d_ff_3_q), .out(subtractor_2_out));  // open: bin, bout
  Decoder #(.select(2), .disabled(0)) decoder_8 (
    .out0(decoder_8_out0), .out1(decoder_8_out1), .out2(decoder_8_out2), .out3(decoder_8_out3),
    .sel(d_ff_8_q), .en(d_ff_10_q));
  D_Flip_Flop d_ff_10 (.clk(clock_4_out), .D(d_ff_6_q), .Q(d_ff_10_q));  // open: Qn, preset, en, reset
  and and_37 (and_37_out, ~and_5_out, register_17_q);  // AND_Gate
  Register #(.width(1)) register_17 (.D(or_22_out), .Q(register_17_q), .clk(or_22_out), .clr(or_17_out));  // open: en
  or or_15 (or_15_out, decoder_9_out3, decoder_9_out2, decoder_9_out1, register_19_q);
  LED led_31 (.in(decoder_8_out2));
  Decoder #(.select(2), .disabled(0), .enable("false")) decoder_9 (
    .out1(decoder_9_out1), .out2(decoder_9_out2), .out3(decoder_9_out3), .sel(out_6));  // open: out0
  Multiplexer #(.width(2), .disabled(0)) multiplexer_7 (
    .in0(subtractor_1_out), .in1(subtractor_2_out), .out(out_6), .sel(multiplexer_3_out), .en(and_37_out));
  LED led_32 (.in(decoder_8_out3));
  Subtractor #(.width(2)) subtractor_3 (
    .a(d_ff_8_q), .b(multiplexer_5_out), .out(subtractor_3_out));  // open: bin, bout
  Subtractor #(.width(2)) subtractor_4 (
    .a(multiplexer_5_out), .b(d_ff_8_q), .out(subtractor_4_out));  // open: bin, bout
  or or_16 (or_16_out, decoder_10_out3, decoder_10_out2, decoder_10_out1, register_20_q);
  Multiplexer #(.width(2), .disabled(0)) multiplexer_8 (
    .in0(subtractor_3_out), .in1(subtractor_4_out), .out(out_5), .sel(multiplexer_6_out), .en(and_38_out));
  and and_38 (and_38_out, ~and_10_out, register_18_q);  // AND_Gate
  Register #(.width(1)) register_18 (.D(or_24_out), .Q(register_18_q), .clk(or_24_out), .clr(or_19_out));  // open: en
  LED led_33 (.in(decoder_11_out0));
  Counter #(.width(4), .max('h6)) counter_3 (
    .load(and_39_out), .count(decoder_9_out1), .Q(counter_3_q), .clk(clock_5_out), .clr(1'b0));  // open: D, carry
  Clock clock_5 (.out(clock_5_out));
  Counter #(.width(4), .max('hb)) counter_4 (
    .load(and_40_out), .count(decoder_9_out2), .Q(counter_4_q), .clk(clock_6_out), .clr(1'b0));  // open: D, carry
  Clock clock_6 (.out(clock_6_out));
  Counter #(.width(5), .max('h16)) counter_5 (
    .load(and_41_out), .count(decoder_9_out3), .Q(counter_5_q), .clk(clock_7_out), .clr(1'b0));  // open: D, carry
  Clock clock_7 (.out(clock_7_out));
  Decoder #(.select(2), .disabled(0), .enable("false")) decoder_10 (
    .out1(decoder_10_out1), .out2(decoder_10_out2), .out3(decoder_10_out3), .sel(out_5));  // open: out0
  LED led_34 (.in(decoder_11_out1));
  and and_39 (and_39_out, counter_3_q[0], counter_3_q[2]);
  and and_40 (and_40_out, counter_4_q[1], counter_4_q[3]);
  and and_41 (and_41_out, counter_5_q[0], counter_5_q[1], counter_5_q[2], counter_5_q[3]);
  LED led_35 (.in(decoder_12_out0));
  Counter #(.width(4), .max('h6)) counter_6 (
    .load(and_42_out), .count(decoder_10_out1), .Q(counter_6_q), .clk(clock_8_out), .clr(1'b0));  // open: D, carry
  Clock clock_8 (.out(clock_8_out));
  Counter #(.width(4), .max('hb)) counter_7 (
    .load(and_43_out), .count(decoder_10_out2), .Q(counter_7_q), .clk(clock_9_out), .clr(1'b0));  // open: D, carry
  Clock clock_9 (.out(clock_9_out));
  Counter #(.width(5), .max('h16)) counter_8 (
    .load(and_44_out), .count(decoder_10_out3), .Q(counter_8_q), .clk(clock_10_out), .clr(1'b0));  // open: D, carry
  Clock clock_10 (.out(clock_10_out));
  Decoder #(.select(2), .disabled(0)) decoder_11 (
    .out0(decoder_11_out0), .out1(decoder_11_out1), .out2(decoder_11_out2), .out3(decoder_11_out3),
    .sel(d_ff_3_q), .en(or_22_out));
  LED led_36 (.in(decoder_12_out1));
  and and_42 (and_42_out, counter_6_q[0], counter_6_q[2]);
  and and_43 (and_43_out, counter_7_q[1], counter_7_q[3]);
  and and_44 (and_44_out, counter_8_q[0], counter_8_q[1], counter_8_q[2], counter_8_q[3]);
  LED led_37 (.in(decoder_11_out2));
  or or_17 (or_17_out, and_39_out, and_40_out, and_41_out);
  Decoder #(.select(2), .disabled(0)) decoder_12 (
    .out0(decoder_12_out0), .out1(decoder_12_out1), .out2(decoder_12_out2), .out3(decoder_12_out3),
    .sel(d_ff_8_q), .en(or_24_out));
  LED led_38 (.in(decoder_11_out3));
  Register #(.width(1)) register_19 (.D(or_17_out), .Q(register_19_q), .clk(or_17_out), .clr(or_18_out));  // open: en
  or or_18 (or_18_out, button_10_out, and_46_out);
  LED led_39 (.in(decoder_12_out2));
  or or_19 (or_19_out, and_42_out, and_43_out, and_44_out);
  Counter #(.width(4), .max('hb)) counter_9 (
    .load(and_46_out), .count(register_19_q), .Q(counter_9_q), .clk(clock_11_out), .clr(or_20_out));  // open: D, carry
  Clock clock_11 (.out(clock_11_out));
  or or_20 (or_20_out, button_9_out, button_10_out, 1'b0);
  Button button_9 (.out(button_9_out));
  Button button_10 (.out(button_10_out));
  D_Flip_Flop d_ff_11 (.D(register_19_q), .Q(d_ff_11_q));  // open: clk, Qn, preset, en, reset
  LED led_40 (.in(decoder_12_out3));
  Register #(.width(1)) register_20 (.D(or_19_out), .Q(register_20_q), .clk(or_19_out), .clr(or_21_out));  // open: en
  or or_21 (or_21_out, button_12_out, and_48_out);
  and and_45 (and_45_out, counter_9_q[0], counter_9_q[3]);
  and and_46 (and_46_out, counter_9_q[1], counter_9_q[3]);
  and and_47 (and_47_out, button_10_out, d_ff_11_q);
  Counter #(.width(4), .max('hb)) counter_10 (
    .load(and_48_out), .count(register_20_q), .Q(counter_10_q), .clk(clock_12_out), .clr(or_23_out));  // open: D, carry
  Clock clock_12 (.out(clock_12_out));
  Button button_11 (.out(button_11_out));
  Button button_12 (.out(button_12_out));
  Comparator #(.width(2), .mode("unsigned")) comparator_1 (.a(out_6), .b(in_3), .gt(comparator_1_gt));  // open: eq, lt
  Register #(.width(1)) register_21 (.D(or_22_out), .Q(register_21_q), .clk(or_22_out), .clr(or_17_out));  // open: en
  or or_22 (or_22_out, and_46_out, and_47_out);
  and and_48 (and_48_out, counter_10_q[1], counter_10_q[3]);
  or or_23 (or_23_out, button_11_out, button_12_out, 1'b0);
  D_Flip_Flop d_ff_12 (.D(register_20_q), .Q(d_ff_12_q));  // open: clk, Qn, preset, en, reset
  and and_49 (and_49_out, comparator_1_gt, register_21_q);
  LED led_41 (.in(and_45_out));
  Comparator #(.width(2), .mode("unsigned")) comparator_2 (.a(out_5), .b(in_1), .gt(comparator_2_gt));  // open: eq, lt
  and and_50 (and_50_out, counter_10_q[0], counter_10_q[3]);
  or or_24 (or_24_out, and_48_out, and_51_out);
  and and_51 (and_51_out, button_12_out, d_ff_12_q);
  LED led_42 (.in(and_49_out));
  Register #(.width(1)) register_22 (.D(or_24_out), .Q(register_22_q), .clk(or_24_out), .clr(or_19_out));  // open: en
  and and_52 (and_52_out, comparator_2_gt, register_22_q);
  LED led_43 (.in(and_50_out));
  LED led_44 (.in(and_52_out));

  // Notes on the sheet:
  //   Floor 4
  //   Floor 3
  //   Floor 2
  //   Floor 1
  //   Floor 4
  //   Floor 3
  //   Floor 2
  //   Floor 1
  //   PRESENT FLOOR
  //   Door 1
  //   PRESENT FLOOR
  //   Door 2
  //   OPEN DOOR
  //   UP/DOWN
  //   Door 1
  //   Door 3
  //   Door 2
  //   UP/DOWN
  //   Door 4
  //   OPEN DOOR
  //   Door 3
  //   Door 4
  //   Door 1
  //   Door 2
  //   1 FLOOR TO DO
  //   2 FLOOR TO DO
  //   3 FLOOR TO DO
  //   Door 1
  //   CLOSE DOOR
  //   Door 2
  //   1 FLOOR TO DO
  //   2 FLOOR TO DO
  //   3 FLOOR TO DO
  //   Door 3
  //   CLOSE DOOR
  //   Door 4
  //   Door 3
  //   Door 4
  //   Motor
  //   Motor
endmodule
